# Fritzing sketch Esquemageneral (saved by Fritzing 0.8.5b)
breadboards: 1

parts:
  Raspberry_Pi_1 = Raspberry Pi 3 [part_number=RPI-3-V1.2]
  DHT1 = DHT22 Humidity and Temperature Sensor
  PIR1 = PIR sensor
  Parte4 = Adafruit FONA 808 Breakout [part_number="Adafruit #2542"]
  BATT1 = LiPoly Battery (1300mAh)
  SW-1 = Vibration sensor module
  BATT2 = LiPoly Battery (1300mAh)
  TTP223B2 = TTP223B Capacitive Touch Sensor Module
  Stepdown_Voltage1 = Polulu Stepdown Voltage [part_number=D24V25F3,D24V25F5]
  R1 = Resistor [tolerance=±5% resistance=220 package=THT]
  Solar_Cell1 = 5V 100mA Polycrystalline PET Solar Cell [part_number=IM130407002]  # not connected
  D1 = Rectifier Diode [part_number=1N4001 package="300 mil [THT]"]
  S1 = Toggle Switch [package=THT]

nets:
  VCC: Raspberry_Pi_1.3v3, DHT1.VDD, SW-1.vcc, TTP223B2.VCC, R1.Pin_0
  N1: Raspberry_Pi_1.GIPO4, DHT1.DATA, R1.Pin_1
  GND: Raspberry_Pi_1.GND, Raspberry_Pi_1.GIPO22, DHT1.GND, PIR1.GND, Parte4.GND, SW-1.Ground, SW-1.Digital_output, TTP223B2.GND
  N2: Raspberry_Pi_1.GIPO17, PIR1.SIG
  N3: Raspberry_Pi_1.GIPO27, TTP223B2.SIG
  N4: Raspberry_Pi_1.GIPO15, Parte4.TXD
  N5: Raspberry_Pi_1.GIPO14, Parte4.RXD
  5V: Raspberry_Pi_1.5V, PIR1.VDD, Parte4.+5V, Stepdown_Voltage1.VOut
  N6: BATT1.positive, S1.L2
  N7: BATT1.negative, BATT2.negative
  N8: BATT2.positive, D1.anode
  N9: D1.cathode, S1.COM

notes:
  Regulador
  + |
  +  -
  Vpanel
  Vbat
  Vcarga

custom parts:
  Adafruit FONA 808 Breakout: Cellular + GPS tracking, all in one? Oh yes! Introducing Adafruit FONA 808 MiniGSM + GPS, an all-in-one cellular phone module with that lets you add location-tracking, voice, text, SMS and data to your project in an adorable little package.
  LiPoly Battery (1300mAh): Lithium Ion Polymer Battery (1300mAh)
  Vibration sensor module: Single-roller type full induction trigger switch. When no vibration or tilt, the product is ON conduction state, and in the steady state, when a vibration or tilt, the switch will be rendered instantly disconnect the conductive resistance increases, generating a current pulse signal, thereby triggering circuit. The default state of the swith is close Digital output Supply voltage:3.3V-5V On-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
  TTP223B Capacitive Touch Sensor Module: The TTP223B capacitive touch sensor module uses the TTP223B IC. The appropriate voltage is approximately 2 to 5.5 volts.
  Polulu Stepdown Voltage: Polulu Stepdown Voltage 3V3 or 5V, 2.5A
  5V 100mA Polycrystalline PET Solar Cell: This is 5V 100mA Polycrystalline PET Solar Cell. It is high quality and exquisite appearance. It is used in all kinds of high-grade electronic products.
